// Digital circuit SAP-1.dig as structural Verilog
module SAP_1 (
  input  clk,
  input  AO,
  input  AI,
  input  BO,
  input  BI,
  input  IO,
  input  II,
  input  HALT,
  input  EO,
  input  FI,
  input  SU,
  input  MI,
  input  PROG_in,
  input  RO,
  input  RI,
  input  CO,
  input  CE,
  input  J,
  input  clk_2,
  input  OI
);

  wire alu_1_p5, alu_1_p8, alu_1_p9, and_1_out, Buffer_read, CLK_t, CLR_2_out, CLR_3_out, CLR_4_out,
       CLR_6_out, CLR_7_out, CLR_out, Program_out, STEP_2_out, STEP_out;
  wire [3:0] output_register_1_sel_digit, program_counter_1_leds, register_instruction_1_p6,
       register_mad_1_a_out;
  wire [7:0] dipswitch_1_out, output_register_1_display_out, register_a_1_a_out, register_a_1_bus,
       register_b_1_b_out;

  and and_1 (and_1_out, AO, BO, RO, IO, EO);
  and and_2 (Buffer_read, and_1_out, CO);
  Button STEP (.out(STEP_out));
  Reset #(.invertOutput("false")) CLR (.out(CLR_out));
  LED led_1 (.in(register_a_1_a_out[7]));
  Reset #(.invertOutput("false")) CLR_2 (.out(CLR_2_out));
  LED led_2 (.in(register_b_1_b_out[7]));
  LED led_3 (.in(register_b_1_b_out[6]));
  Reset #(.invertOutput("false")) CLR_3 (.out(CLR_3_out));
  Reset #(.invertOutput("false")) CLR_4 (.out(CLR_4_out));
  clock_module clock_module_1 (
    .HLT(HALT), .STEP_EN(STEP_2_out), .STEP_in(STEP_out), .CLK_in(clk), .CLK(CLK_t));  // open: CLK_2
  DipSwitch STEP_2 (.out(STEP_2_out));
  register_A register_a_1 (
    .CLK(CLK_t), .AO(AO), .AI(AI), .CLR(CLR_out), .BUS(register_a_1_bus[0]), .A_out(register_a_1_a_out));
  LED led_4 (.in(register_a_1_a_out[6]));
  LED led_5 (.in(register_a_1_a_out[5]));
  register_B register_b_1 (
    .CLK(CLK_t), .BO(BO), .BI(BI), .CLR(CLR_2_out), .BUS(register_a_1_bus[0]), .B_out(register_b_1_b_out));
  LED led_6 (.in(register_b_1_b_out[5]));
  LED led_7 (.in(register_b_1_b_out[4]));
  // register_Instruction register_instruction_1: pin names not known; wires that end beside it: CLK_t, IO, II, CLR_3_out, register_a_1_bus, register_instruction_1_p6
  LED led_8 (.in(program_counter_1_leds[2]));
  LED led_9 (.in(program_counter_1_leds[3]));
  program_counter program_counter_1 (
    .CO(CO), .CLK(CLK_t), .CLR(CLR_4_out), .CE(CE), .J(J), .LEDs(program_counter_1_leds),
    .Bus(register_a_1_bus));
  LED led_10 (.in(register_a_1_a_out[4]));
  LED led_11 (.in(register_a_1_a_out[3]));
  LED led_12 (.in(register_b_1_b_out[3]));
  LED led_13 (.in(register_b_1_b_out[2]));
  LED led_14 (.in(register_instruction_1_p6[3]));
  LED led_15 (.in(register_instruction_1_p6[2]));
  LED led_16 (.in(program_counter_1_leds[0]));
  LED led_17 (.in(program_counter_1_leds[1]));
  LED led_18 (.in(CLK_t));
  LED led_19 (.in(register_a_1_a_out[2]));
  LED led_20 (.in(register_a_1_a_out[1]));
  LED led_21 (.in(register_b_1_b_out[1]));
  LED led_22 (.in(register_b_1_b_out[0]));
  LED led_23 (.in(register_instruction_1_p6[1]));
  LED led_24 (.in(register_instruction_1_p6[0]));
  LED led_25 (.in(register_a_1_a_out[0]));
  // ALU alu_1: pin names not known; wires that end beside it: CLK_t, EO, register_b_1_b_out, SU, alu_1_p5, FI, register_a_1_a_out, alu_1_p8, alu_1_p9, register_a_1_bus
  Reset #(.invertOutput("false")) CLR_5 (.out(alu_1_p5));
  DipSwitch dipswitch_1 (.out(dipswitch_1_out[7]));
  DipSwitch dipswitch_2 (.out(dipswitch_1_out[6]));
  DipSwitch dipswitch_3 (.out(dipswitch_1_out[5]));
  register_MAD register_mad_1 (
    .MI(MI), .CLK(CLK_t), .CLR(CLR_6_out), .PROG_in(PROG_in), .Bus_in(register_a_1_bus),
    .A_out(register_mad_1_a_out));  // open: PROG_out
  Reset #(.invertOutput("false")) CLR_6 (.out(CLR_6_out));
  DipSwitch dipswitch_4 (.out(dipswitch_1_out[4]));
  DipSwitch dipswitch_5 (.out(dipswitch_1_out[3]));
  DipSwitch dipswitch_6 (.out(dipswitch_1_out[2]));
  Button #(.activeLow("true")) Program (.out(Program_out));
  DipSwitch dipswitch_7 (.out(dipswitch_1_out[1]));
  DipSwitch dipswitch_8 (.out(dipswitch_1_out[0]));
  LED CF (.in(alu_1_p8));
  LED ZF (.in(alu_1_p9));
  RAM ram_1 (
    .A_in(register_mad_1_a_out), .RO(RO), .PROG(PROG_in), .CLK(CLK_t), .RI(RI), .Trig_Prog(Program_out),
    .D_Prog(dipswitch_1_out), .Bus(register_a_1_bus));
  LED led_26 (.in(register_mad_1_a_out[3]));
  LED led_27 (.in(register_mad_1_a_out[2]));
  LED led_28 (.in(register_mad_1_a_out[1]));
  LED led_29 (.in(register_mad_1_a_out[0]));
  output_register output_register_1 (
    .Refresh_display(clk_2), .OI(OI), .CLK(CLK_t), .CLR(CLR_7_out), .Bus(register_a_1_bus),
    .SEL_digit(output_register_1_sel_digit), .Display_out(output_register_1_display_out));
  Reset #(.invertOutput("false")) CLR_7 (.out(CLR_7_out));
  Seven_Seg #(.commonCathode("true")) seven_seg_1 (
    .a(output_register_1_display_out[0]), .b(output_register_1_display_out[1]),
    .c(output_register_1_display_out[2]), .d(output_register_1_display_out[3]),
    .e(output_register_1_display_out[4]), .f(output_register_1_display_out[5]),
    .g(output_register_1_display_out[6]), .dp(output_register_1_display_out[7]),
    .common(output_register_1_sel_digit[3]));
  Seven_Seg #(.commonCathode("true")) seven_seg_2 (
    .a(output_register_1_display_out[0]), .b(output_register_1_display_out[1]),
    .c(output_register_1_display_out[2]), .d(output_register_1_display_out[3]),
    .e(output_register_1_display_out[4]), .f(output_register_1_display_out[5]),
    .g(output_register_1_display_out[6]), .dp(output_register_1_display_out[7]),
    .common(output_register_1_sel_digit[2]));
  Seven_Seg #(.commonCathode("true")) seven_seg_3 (
    .a(output_register_1_display_out[0]), .b(output_register_1_display_out[1]),
    .c(output_register_1_display_out[2]), .d(output_register_1_display_out[3]),
    .e(output_register_1_display_out[4]), .f(output_register_1_display_out[5]),
    .g(output_register_1_display_out[6]), .dp(output_register_1_display_out[7]),
    .common(output_register_1_sel_digit[1]));
  Seven_Seg #(.commonCathode("true")) seven_seg_4 (
    .a(output_register_1_display_out[0]), .b(output_register_1_display_out[1]),
    .c(output_register_1_display_out[2]), .d(output_register_1_display_out[3]),
    .e(output_register_1_display_out[4]), .f(output_register_1_display_out[5]),
    .g(output_register_1_display_out[6]), .dp(output_register_1_display_out[7]),
    .common(output_register_1_sel_digit[0]));
  // Pins of 1 and 8 bits meet at register_a_1_bus

  // Notes on the sheet:
  //   AO: default 1
  //   AI: default 1
  //   BO: default 1
  //   BI: default 1
  //   IO: default 1
  //   II: default 1
  //   EO: default 1
  //   FI: default 1
  //   MI: default 1
  //   PROG_in: default 1
  //   RO: default 1
  //   CO: default 1
  //   J: default 1
  //   clk_2: Hz: 100
  //   Clock
  //   A Register
  //   B Register
  //   Instruction Register
  //   Program Counter
  //   ALU
  //   Memory Address Register
  //   RAM
  //   Output Register
endmodule
